// Logisim project Labo4.circ as structural Verilog: 4 circuits, main circuit LatchD
module LatchD (
  input  D,
  input  LD,
  output Q,
  output Q2
);

  wire and_1_out, and_2_out, not_1_out;

  not not_1 (not_1_out, D);
  and and_1 (and_1_out, not_1_out, LD);
  and and_2 (and_2_out, LD, D);
  nor nor_1 (Q, and_1_out, Q2);
  nor nor_2 (Q2, Q, and_2_out);

  // Notes on the sheet:
  //   Attention, votre version de Logisim
  //   ne contient pas de tracker. Si vous
  //   enregistrez votre projet, toutes les
  //   informations du tracker seront
  //   définitivement effacées.
endmodule

module FlipFlop (
  input  D,
  input  CK,
  output Q,
  output Q2
);

  wire Maitre_q, not_1_out, not_2_out;

  not not_1 (not_1_out, CK);
  LatchD Maitre (.D(D), .LD(not_1_out), .Q(Maitre_q));  // open: Q2
  not not_2 (not_2_out, not_1_out);
  LatchD latchd_1 (.D(Maitre_q), .LD(not_2_out), .Q(Q), .Q2(Q2));

  // Notes on the sheet:
  //   Attention, votre version de Logisim
  //   ne contient pas de tracker. Si vous
  //   enregistrez votre projet, toutes les
  //   informations du tracker seront
  //   définitivement effacées.
endmodule

module ShiftRegistre4bits (
  input  D3,
  input  D2,
  input  D1,
  input  D0,
  input  L,
  input  R,
  input  [1:0] S,
  input  CK,
  output Q3,
  output Q2,
  output Q1,
  output Q0
);

  wire multiplexer_1_out, multiplexer_2_out, multiplexer_3_out, multiplexer_4_out;

  Multiplexer #(.select(2), .enable("false")) multiplexer_1 (
    .in0(Q3), .in1(Q2), .in2(D3), .in3(R), .out(multiplexer_1_out), .sel(S));
  D_Flip_Flop d_ff_1 (.D(multiplexer_1_out), .clk(CK), .Q(Q3));  // open: Qn, preset, reset
  Multiplexer #(.select(2), .enable("false")) multiplexer_2 (
    .in0(Q2), .in1(Q1), .in2(D2), .in3(Q3), .out(multiplexer_2_out), .sel(S));
  D_Flip_Flop d_ff_2 (.D(multiplexer_2_out), .clk(CK), .Q(Q2));  // open: Qn, preset, reset
  Multiplexer #(.select(2), .enable("false")) multiplexer_3 (
    .in0(Q1), .in1(Q0), .in2(D1), .in3(Q2), .out(multiplexer_3_out), .sel(S));
  D_Flip_Flop d_ff_3 (.D(multiplexer_3_out), .clk(CK), .Q(Q1));  // open: Qn, preset, reset
  Multiplexer #(.select(2), .enable("false")) multiplexer_4 (
    .in0(Q0), .in1(L), .in2(D0), .in3(Q1), .out(multiplexer_4_out), .sel(S));
  D_Flip_Flop d_ff_4 (.D(multiplexer_4_out), .clk(CK), .Q(Q0));  // open: Qn, preset, reset

  // Notes on the sheet:
  //   Attention, votre version de Logisim
  //   ne contient pas de tracker. Si vous
  //   enregistrez votre projet, toutes les
  //   informations du tracker seront
  //   définitivement effacées.
endmodule

module ShiftRegistre8bits (
  input  [1:0] S,
  input  CK,
  input  L,
  input  R,
  input  [7:0] in_5,
  output [7:0] out_6
);

  ShiftRegistre4bits shiftregistre4bits_1 (
    .D3(in_5[3]), .D2(in_5[2]), .D1(in_5[1]), .D0(in_5[0]), .L(L), .R(out_6[4]), .S(S), .CK(CK),
    .Q3(out_6[3]), .Q2(out_6[2]), .Q1(out_6[1]), .Q0(out_6[0]));
  ShiftRegistre4bits shiftregistre4bits_2 (
    .D3(in_5[7]), .D2(in_5[6]), .D1(in_5[5]), .D0(in_5[4]), .L(out_6[3]), .R(R), .S(S), .CK(CK),
    .Q3(out_6[7]), .Q2(out_6[6]), .Q1(out_6[5]), .Q0(out_6[4]));

  // Notes on the sheet:
  //   Attention, votre version de Logisim
  //   ne contient pas de tracker. Si vous
  //   enregistrez votre projet, toutes les
  //   informations du tracker seront
  //   définitivement effacées.
endmodule
