// Logisim project labo4.circ as structural Verilog: 7 circuits, main circuit CHRONO_SHREGI_8BITS
module SHREGI_4BITS (
  input  [3:0] D,
  input  R,
  input  L,
  input  [1:0] S,
  input  CLR,
  input  CLK,
  output [3:0] Q
);

  wire multiplexer_1_out, multiplexer_2_out, multiplexer_3_out, multiplexer_4_out;

  Multiplexer #(.select(2), .enable("false")) multiplexer_1 (
    .in0(Q[3]), .in1(D[3]), .in2(Q[2]), .in3(R), .out(multiplexer_1_out), .sel(S));
  D_Flip_Flop d_ff_1 (.D(multiplexer_1_out), .clk(CLK), .Q(Q[3]), .reset(CLR));  // open: Qn, preset
  Multiplexer #(.select(2), .enable("false")) multiplexer_2 (
    .in0(Q[2]), .in1(D[2]), .in2(Q[1]), .in3(Q[3]), .out(multiplexer_2_out), .sel(S));
  D_Flip_Flop d_ff_2 (.D(multiplexer_2_out), .clk(CLK), .Q(Q[2]), .reset(CLR));  // open: Qn, preset
  Multiplexer #(.select(2), .enable("false")) multiplexer_3 (
    .in0(Q[1]), .in1(D[1]), .in2(Q[0]), .in3(Q[2]), .out(multiplexer_3_out), .sel(S));
  D_Flip_Flop d_ff_3 (.D(multiplexer_3_out), .clk(CLK), .Q(Q[1]), .reset(CLR));  // open: Qn, preset
  Multiplexer #(.select(2), .enable("false")) multiplexer_4 (
    .in0(Q[0]), .in1(D[0]), .in2(L), .in3(Q[1]), .out(multiplexer_4_out), .sel(S));
  D_Flip_Flop d_ff_4 (.D(multiplexer_4_out), .clk(CLK), .Q(Q[0]), .reset(CLR));  // open: Qn, preset

  // Notes on the sheet:
  //   Attention, votre version de Logisim
  //   ne contient pas de tracker. Si vous
  //   enregistrez votre projet, toutes les
  //   informations du tracker seront
  //   définitivement effacées.
endmodule

module SHREGI_8BITS (
  input  [1:0] in_1,
  input  [7:0] D,
  input  CLR,
  output [7:0] Q
);

  wire bitselector_1_out, bitselector_2_out, CLK_out;

  Clock CLK (.out(CLK_out));
  SHREGI_4BITS shregi_4bits_1 (
    .D(D[3:0]), .R(bitselector_1_out), .L(1'b0), .S(in_1), .CLR(CLR), .CLK(CLK_out), .Q(Q[3:0]));
  SHREGI_4BITS shregi_4bits_2 (
    .D(D[7:4]), .R(1'b0), .L(bitselector_2_out), .S(in_1), .CLR(CLR), .CLK(CLK_out), .Q(Q[7:4]));
  BitSelector #(.width(4)) bitselector_1 (.in(Q[7:4]), .out(bitselector_1_out), .sel(2'b00));
  BitSelector #(.width(4)) bitselector_2 (.in(Q[3:0]), .out(bitselector_2_out), .sel(2'b11));

  // Notes on the sheet:
  //   Attention, votre version de Logisim
  //   ne contient pas de tracker. Si vous
  //   enregistrez votre projet, toutes les
  //   informations du tracker seront
  //   définitivement effacées.
endmodule

module LFSR_8BITS (
  input  PR,
  input  CLK,
  output [3:0] Q0,
  output [3:0] Q1
);

  wire xnor_1_out, xnor_2_out, xnor_3_out;

  D_Flip_Flop d_ff_1 (.D(xnor_1_out), .clk(CLK), .Q(Q0[0]), .preset(PR));  // open: Qn, reset
  D_Flip_Flop d_ff_2 (.D(Q0[0]), .clk(CLK), .Q(Q0[1]), .preset(PR));  // open: Qn, reset
  xnor xnor_1 (xnor_1_out, xnor_2_out, Q0[3]);
  xnor xnor_2 (xnor_2_out, xnor_3_out, Q1[0]);
  D_Flip_Flop d_ff_3 (.D(Q0[1]), .clk(CLK), .Q(Q0[2]), .preset(PR));  // open: Qn, reset
  D_Flip_Flop d_ff_4 (.D(Q0[2]), .clk(CLK), .Q(Q0[3]), .preset(PR));  // open: Qn, reset
  xnor xnor_3 (xnor_3_out, Q1[3], Q1[1]);
  D_Flip_Flop d_ff_5 (.D(Q0[3]), .clk(CLK), .Q(Q1[0]), .preset(PR));  // open: Qn, reset
  D_Flip_Flop d_ff_6 (.D(Q1[0]), .clk(CLK), .Q(Q1[1]), .preset(PR));  // open: Qn, reset
  D_Flip_Flop d_ff_7 (.D(Q1[1]), .clk(CLK), .Q(Q1[2]), .preset(PR));  // open: Qn, reset
  D_Flip_Flop d_ff_8 (.D(Q1[2]), .clk(CLK), .Q(Q1[3]), .preset(PR));  // open: Qn, reset

  // Notes on the sheet:
  //   Attention, votre version de Logisim
  //   ne contient pas de tracker. Si vous
  //   enregistrez votre projet, toutes les
  //   informations du tracker seront
  //   définitivement effacées.
endmodule

module LFSRPR0 (
  input  in_1
);

  wire clock_1_out;
  wire [3:0] lfsr_8bits_1_q0, lfsr_8bits_1_q1;

  Clock clock_1 (.out(clock_1_out));
  LFSR_8BITS lfsr_8bits_1 (.PR(in_1), .CLK(clock_1_out), .Q0(lfsr_8bits_1_q0), .Q1(lfsr_8bits_1_q1));
  Hex_Digit_Display hex_digit_display_1 (.value(lfsr_8bits_1_q0));  // open: dp
  Hex_Digit_Display hex_digit_display_2 (.value(lfsr_8bits_1_q1));  // open: dp

  // Notes on the sheet:
  //   Attention, votre version de Logisim
  //   ne contient pas de tracker. Si vous
  //   enregistrez votre projet, toutes les
  //   informations du tracker seront
  //   définitivement effacées.
endmodule

module LFSRPR1 (
);

  wire clock_1_out;
  wire [3:0] lfsr_8bits_1_q0, lfsr_8bits_1_q1;

  Clock clock_1 (.out(clock_1_out));
  LFSR_8BITS lfsr_8bits_1 (.PR(1'b1), .CLK(clock_1_out), .Q0(lfsr_8bits_1_q0), .Q1(lfsr_8bits_1_q1));
  Hex_Digit_Display hex_digit_display_1 (.value(lfsr_8bits_1_q0));  // open: dp
  Hex_Digit_Display hex_digit_display_2 (.value(lfsr_8bits_1_q1));  // open: dp

  // Notes on the sheet:
  //   Attention, votre version de Logisim
  //   ne contient pas de tracker. Si vous
  //   enregistrez votre projet, toutes les
  //   informations du tracker seront
  //   définitivement effacées.
endmodule

module CHRONO_SHREGI_8BITS (
  input  [1:0] in_1,
  output [7:0] Q
);

  wire CLK_out;
  wire [7:0] counter_1_q;

  Clock CLK (.out(CLK_out));
  Clock sysclk ();  // open: out
  Counter counter_1 (
    .clr(1'b0), .load(1'b0), .up(1'b1), .count(1'b1), .clk(CLK_out), .Q(counter_1_q));  // open: D, carry
  SHREGI_8BITS shregi_8bits_1 (.in_1(in_1), .D(counter_1_q), .Q(Q));  // open: CLR

  // Notes on the sheet:
  //   Attention, votre version de Logisim
  //   ne contient pas de tracker. Si vous
  //   enregistrez votre projet, toutes les
  //   informations du tracker seront
  //   définitivement effacées.
endmodule

module CHRONO_LFSR_8BITS (
  output [7:0] out_1
);

  wire CLK_out, counter_1_q;

  Counter #(.width(1), .max('h1)) counter_1 (
    .clr(1'b0), .load(1'b0), .up(1'b1), .count(1'b1), .clk(CLK_out), .Q(counter_1_q));  // open: D, carry
  Clock #(.highDuration(4), .lowDuration(4)) CLK (.out(CLK_out));
  Clock sysclk ();  // open: out
  LFSR_8BITS lfsr_8bits_1 (.CLK(counter_1_q), .Q0(out_1[3:0]), .Q1(out_1[7:4]));  // open: PR

  // Notes on the sheet:
  //   Attention, votre version de Logisim
  //   ne contient pas de tracker. Si vous
  //   enregistrez votre projet, toutes les
  //   informations du tracker seront
  //   définitivement effacées.
endmodule
